# Fritzing sketch schéma plošného spoje (saved by Fritzing 0.9.3b)
circuit board: 5.92279cm x 3.06505cm

parts:
  Krokový_motor = Stepper Motor - Bipolar
  Driver_krokového_motoru = EasyDriver_v44
  R1 = Resistor [tolerance=±5% resistance=220 package=THT]
  R2 = Resistor [tolerance=±5% resistance=220 package=THT]
  Konektor_externího_napájení(12V) = Screw terminal - 2 pins [package=THT]
  Volná_DuPont_lišta_-M = mystery part, 8 pins
  Konektor_nástroje = mystery part, 8 pins [chip_label=?]

nets:
  N1: Krokový_motor.A, Driver_krokového_motoru.OUT1A
  N2: Krokový_motor.C, Driver_krokového_motoru.OUT1B
  N3: Krokový_motor.B, Driver_krokového_motoru.OUT2B
  N4: Krokový_motor.D, Driver_krokového_motoru.OUT2A
  N5: Driver_krokového_motoru.GND, Driver_krokového_motoru.MS1, Driver_krokového_motoru.MS2, Konektor_externího_napájení(12V).pin1, Volná_DuPont_lišta_-M.pin8, Konektor_nástroje.pin8
  N6: Driver_krokového_motoru.V+, Konektor_externího_napájení(12V).pin2, Volná_DuPont_lišta_-M.pin5, Konektor_nástroje.pin5
  N7: Driver_krokového_motoru.STEP, R2.Pin_1, Volná_DuPont_lišta_-M.pin4, Konektor_nástroje.pin4
  N8: Driver_krokového_motoru.DIR, R1.Pin_1, Volná_DuPont_lišta_-M.pin3, Konektor_nástroje.pin3
  N9: Driver_krokového_motoru.VCC, R1.Pin_0, R2.Pin_0
  N10: Volná_DuPont_lišta_-M.pin1, Konektor_nástroje.pin1
  N11: Volná_DuPont_lišta_-M.pin2, Konektor_nástroje.pin2
  N12: Volná_DuPont_lišta_-M.pin6, Konektor_nástroje.pin6
  N13: Volná_DuPont_lišta_-M.pin7, Konektor_nástroje.pin7

// code stored in the sketch: Untitled.ino

